# Fritzing sketch Variometer (saved by Fritzing 0.8.5b)
circuit board: 8.46667cm x 5.64444cm
breadboards: 1

parts:
  Composants1 = Arduino Nano (Rev3.0)
  Composants2 = Barometric Pressure Sensor - BMP085 Breakout
  Nokia_5110_LCD_Module1 = Nokia5110LCDModule
  Composants3 = Real Time Clock Module - DS1307 RTC Breakout Board
  SP1 = SPEAKER [package=pcb_mount_speaker]
  U1 = LIPO-1000mAh [package=lipo-1000]
  Composants4 = USB LiPoly Charger
  S1 = Toggle Switch [package=THT]
  R1 = Resistor [tolerance=±5% resistance=10k package=THT]
  R2 = Resistor [tolerance=±5% resistance=10k package=THT]
  ENCODER1 = Rotary Encoder with Knob
  R3 = Resistor [tolerance=±5% resistance=10k package=THT]
  R4 = Resistor [tolerance=±5% resistance=110 package=THT]
  Composants5 = NCP1400 Step-Up Breakout
  R5 = Resistor [tolerance=±5% resistance=100k package=THT]

nets (from the breadboard view):
  N1: Composants1.D2, R1.Pin_1, ENCODER1.no_name_yet#3
  N2: Composants1.D3, R2.Pin_1, ENCODER1.no_name_yet#1
  N3: Composants1.D5, Nokia_5110_LCD_Module1.D/C
  N4: Composants1.D6, Nokia_5110_LCD_Module1.RST
  N5: Composants1.D7, Nokia_5110_LCD_Module1.SCE
  N6: Composants1.D8, Nokia_5110_LCD_Module1.SCLK
  N7: Composants1.D9, R4.Pin_1
  N8: Composants1.D10, SP1.+
  N9: Composants1.D11/MOSI, Nokia_5110_LCD_Module1.LED
  N10: Composants1.D12/MISO, ENCODER1.no_name_yet#5, R3.Pin_1
  GND: Composants1.GND, Composants2.GND, Nokia_5110_LCD_Module1.Grnd, Composants3.GND, ENCODER1.no_name_yet#2, ENCODER1.no_name_yet#4
  5V: Composants1.5V, Composants3.5V, R1.Pin_0, R2.Pin_0, R3.Pin_0, Composants5.VOUT
  N11: Composants1.A4, Composants2.SDA, Composants3.SDA
  N12: Composants1.A0, R5.Pin_0
  VCC: Composants1.3V3, Composants2.VCC, Nokia_5110_LCD_Module1.Vcc
  N13: Composants2.SCL, Composants3.SCL
  N14: SP1.-, R4.Pin_0
  N15: U1.+, Composants4.VBAT, S1.COM
  GND_2: U1.-, Composants4.GND, Composants5.GND
  N16: S1.L2, Composants5.VIN, R5.Pin_1

custom parts:
  : Nokia 5110 LCD with 8 pin. It's a 45mm*45mm module part. Description: The Nokia 5110 is a basic graphic LCD screen for lots of applications. It was originally intended for as a cell phone screen. This one is mounted on an easy to solder PCB. It uses the PCD8544 controller. The PCD8544 is a low power CMOS LCD controller/driver, designed to drive a graphic display of 48 rows and 84 columns. All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
  Rotary Encoder with Knob: Rotary Encoder with 1/4" Shaft and Knob
